# Fritzing sketch circuit (saved by Fritzing 0.9.3b)
breadboards: 1

parts:
  R1 = Resistor [tolerance=±5% resistance=220 package=THT]
  LED1 = LED - 5mm [color="Red (633nm)" package="5 mm [THT]"]
  Part1 = Arduino Uno (Rev3)
  Part2 = TRRS 3.5mm Jack Breakout

nets:
  N1: R1.Pin_0, LED1.cathode
  N2: R1.Pin_1, Part1.GND
  N3: LED1.anode, Part1.D0/RX
  N4: Part1.A0, Part2.SLEEVE
  N5: Part1.A1, Part2.RING2
  N6: Part1.A2, Part2.RING1
  N7: Part1.A3, Part2.TIP
